// Logisim project conditional_swapper.circ as structural Verilog: 1 circuit, main circuit Conditional Swapper
// csw
module Conditional_Swapper (
  input  [15:0] B,
  input  [15:0] A,
  output [15:0] B_2,
  output B_A,
  output [15:0] A_2
);

  comparator comparator_1 (.A_B(B_A), .A(A), .B(B));
  Multiplexer #(.width(16), .enable("false")) multiplexer_1 (.in0(A), .in1(B), .out(B_2), .sel(B_A));
  Multiplexer #(.width(16), .enable("false")) multiplexer_2 (.in0(B), .in1(A), .out(A_2), .sel(B_A));
endmodule
